// Logisim project 4.circ as structural Verilog: 2 circuits, main circuit main
module main (
  input  in_1,
  input  in_2,
  input  in_3,
  input  in_4,
  input  in_5,
  input  in_6,
  input  in_7,
  input  in_8,
  input  in_9
);

  wire xor_4_out;

  // XOR_Gate xor_1 has open pins: in0=in_1, in1=in_2, out=open
  FullAdder fulladder_1 (.A(in_3));  // open: B, Cin, S, Cout
  // XOR_Gate xor_2 has open pins: in0=in_1, in1=in_4, out=open
  // XOR_Gate xor_3 has open pins: in0=in_1, in1=in_6, out=open
  FullAdder fulladder_2 (.A(in_5));  // open: B, Cin, S, Cout
  xor xor_4 (xor_4_out, in_1, in_8);
  FullAdder fulladder_3 (.A(in_7));  // open: B, Cin, S, Cout
  FullAdder fulladder_4 (.A(in_9), .B(xor_4_out));  // open: Cin, S, Cout
endmodule

module FullAdder (
  input  A,
  input  B,
  input  Cin,
  output S,
  output Cout
);

  wire and_1_out, and_2_out, xor_1_out;

  xor xor_1 (xor_1_out, A, B);
  and and_1 (and_1_out, Cin, xor_1_out);
  and and_2 (and_2_out, A, B);
  xor xor_2 (S, xor_1_out, Cin);
  or or_1 (Cout, and_1_out, and_2_out);
endmodule
